// Logisim project trab.circ as structural Verilog: 1 circuit, main circuit main
module main (
  input  A,
  input  B,
  input  C,
  input  D,
  output F,
  output G,
  output H,
  output i,
  output J,
  output K,
  output L,
  output M,
  output N,
  output O,
  output P,
  output Q,
  output R,
  output out_18,
  output T,
  output U,
  output V,
  output W,
  output X,
  output Y,
  output Z
);

  wire and_2_out, and_3_out, and_4_out, and_5_out, and_6_out, and_7_out, and_8_out, and_9_out, and_10_out,
       and_11_out, and_12_out, and_13_out, and_14_out, and_15_out, and_16_out, and_17_out, and_18_out,
       and_19_out, and_20_out, and_21_out, and_22_out, and_23_out, and_24_out, and_25_out, and_26_out,
       and_27_out, nand_5_out, nand_6_out, nor_2_out, not_2_out, not_3_out, or_3_out, or_4_out, or_5_out,
       or_6_out, or_7_out, or_8_out, or_9_out, or_10_out, or_11_out, or_12_out, xor_1_out;

  not not_1 (G, B);
  not not_2 (not_2_out, A);
  not not_3 (not_3_out, C);
  not not_4 (N, D);
  and and_1 (F, G, not_2_out);
  or or_1 (H, not_2_out, A);
  nand nand_1 (i, G, A);
  nand nand_2 (J, B, not_2_out);
  nor nor_1 (M, D, C);
  or or_2 (O, not_2_out, A);
  nand nand_3 (P, N, C);
  nand nand_4 (out_18, D, not_3_out);
  nor nor_2 (nor_2_out, D, C);
  and and_2 (and_2_out, D, C);
  and and_3 (and_3_out, C, A);
  or or_3 (or_3_out, D, C);
  nand nand_5 (nand_5_out, D, C);
  nand nand_6 (nand_6_out, N, C);
  or or_4 (or_4_out, N, C);
  xor xor_1 (xor_1_out, C, D);
  and and_4 (and_4_out, C, G);
  and and_5 (and_5_out, N, G);
  and and_6 (and_6_out, D, not_3_out);
  and and_7 (and_7_out, nand_5_out, G);
  and and_8 (and_8_out, not_3_out, B);
  and and_9 (and_9_out, nand_6_out, G);
  and and_10 (and_10_out, or_4_out, B);
  and and_11 (and_11_out, or_4_out, G);
  and and_12 (and_12_out, xor_1_out, B);
  and and_13 (and_13_out, nor_2_out, G);
  and and_14 (and_14_out, and_2_out, B);
  and and_15 (and_15_out, or_3_out, B);
  and and_16 (and_16_out, and_6_out, B);
  and and_17 (and_17_out, or_3_out, G);
  or or_5 (or_5_out, and_11_out, and_12_out);
  or or_6 (or_6_out, and_4_out, and_15_out);
  or or_7 (or_7_out, and_13_out, and_14_out);
  and and_18 (and_18_out, and_15_out, A);
  or or_8 (or_8_out, and_5_out, and_16_out);
  or or_9 (or_9_out, and_7_out, and_8_out);
  or or_10 (or_10_out, and_9_out, and_10_out);
  or or_11 (or_11_out, and_17_out, B);
  and and_19 (and_19_out, or_6_out, not_2_out);
  or or_12 (or_12_out, and_3_out, and_18_out);
  and and_20 (and_20_out, or_8_out, not_2_out);
  and and_21 (and_21_out, or_7_out, A);
  and and_22 (and_22_out, or_9_out, A);
  and and_23 (and_23_out, or_10_out, not_2_out);
  and and_24 (and_24_out, or_11_out, A);
  and and_25 (and_25_out, or_5_out, not_2_out);
  and and_26 (and_26_out, or_10_out, A);
  or or_13 (Y, and_19_out, A);
  and and_27 (and_27_out, or_7_out, not_2_out);
  or or_14 (V, not_2_out, and_22_out);
  or or_15 (W, and_23_out, and_24_out);
  or or_16 (X, and_25_out, and_26_out);
  or or_17 (T, and_27_out, or_12_out);
  or or_18 (U, and_20_out, and_21_out);
  _7_Segment_Display u_7_segment_display_1 (.g(A), .f(F), .a(J), .b(H), .e(G), .d(J), .c(i));  // open: dp
  _7_Segment_Display u_7_segment_display_2 (.g(C), .f(M), .a(out_18), .b(O), .e(N), .d(out_18), .c(P));  // open: dp
  _7_Segment_Display u_7_segment_display_3 (.g(Y), .f(T), .a(X), .b(V), .e(U), .d(X), .c(W));  // open: dp

  assign K = A;
  assign L = J;
  assign Q = out_18;
  assign R = C;
  assign Z = X;
endmodule
